# Fritzing sketch 4_LED_config (saved by Fritzing 0.9.2b)
breadboards: 1

parts:
  R1 = Resistor [tolerance=±5% resistance=220 package=THT]
  R2 = Resistor [tolerance=±5% resistance=220 package=THT]
  R4 = Resistor [tolerance=±5% resistance=220 package=THT]
  R5 = Resistor [tolerance=±5% resistance=220 package=THT]
  Part1 = Arduino BT
  LED1 = smd LED [color="Red (633nm)" package="0805 [SMD]"]
  LED2 = smd LED [color="Red (633nm)" package="0805 [SMD]"]
  LED3 = smd LED [color="Red (633nm)" package="0805 [SMD]"]
  LED4 = smd LED [color="Red (633nm)" package="0805 [SMD]"]

nets:
  N1: R1.Pin_0, Part1.MISO/D12
  N2: R1.Pin_1, LED1.anode
  N3: R2.Pin_0, Part1.SS/PWM_D10
  N4: R2.Pin_1, LED3.anode
  N5: R4.Pin_0, Part1.MOSI/PWM_D11
  N6: R4.Pin_1, LED2.anode
  N7: R5.Pin_0, Part1.PWM_D9
  N8: R5.Pin_1, LED4.anode
  N9: Part1.GND, LED1.cathode, LED2.cathode, LED3.cathode, LED4.cathode
