# Fritzing sketch Stepper_to_Arduino_2 (saved by Fritzing 0.9.2b)
breadboards: 1

parts:
  Part2 = Arduino BT
  R6 = Resistor [tolerance=±5% resistance=220 package=THT]
  R7 = Resistor [tolerance=±5% resistance=220 package=THT]
  R8 = Resistor [tolerance=±5% resistance=220 package=THT]
  R9 = Resistor [tolerance=±5% resistance=220 package=THT]
  LED5 = smd LED [color="Red (633nm)" package="0805 [SMD]"]
  LED6 = smd LED [color="Red (633nm)" package="0805 [SMD]"]
  LED7 = smd LED [color="Red (633nm)" package="0805 [SMD]"]
  LED8 = smd LED [color="Red (633nm)" package="0805 [SMD]"]
  M1 = Stepper Motor - Unipolar
  IC2 = ULN2003A [package="SO16 [SMD]"]

nets:
  N1: Part2.PWM_D9, R9.Pin_0, IC2.In_4
  N2: Part2.SS/PWM_D10, R8.Pin_0, IC2.In_2
  N3: Part2.MOSI/PWM_D11, R7.Pin_0, IC2.In_3
  N4: Part2.MISO/D12, R6.Pin_0, IC2.In_1
  N5: Part2.GND, LED5.cathode, LED6.cathode, LED7.cathode, LED8.cathode, M1.C, IC2.0V
  N6: Part2.5V, M1.D, IC2.COM_-_Common
  N7: R6.Pin_1, LED5.anode
  N8: R7.Pin_1, LED7.anode
  N9: R8.Pin_1, LED6.anode
  N10: R9.Pin_1, LED8.anode
  N11: M1.A, IC2.Out_1
  N12: M1.COMMON_1, IC2.Out_2
  N13: M1.B, IC2.Out_3
  N14: M1.COMMON_2, IC2.Out_4
