# Fritzing sketch Ultrasonic Detector with Servo 1 (saved by Fritzing 0.9.2b)
breadboards: 1

parts:
  J1 = Basic Servo
  Part3 = Arduino Uno (Rev3)

nets:
  GND: J1.gnd, Part3.GND
  VCC: J1.vcc, Part3.5V
  N1: J1.pulse, Part3.D9_PWM

notes:
  There is no HC-SR04 Detector in this program. Wires go:
  Red= VCC
  Orange= Trig (pin:12)
  Green= Echo (pin: 11)
  Black= GND
