# Fritzing sketch Robot1_H-Bridge_PhotoResistorWiring_9Volt (saved by Fritzing 0.9.2b)
breadboards: 1

parts:
  IC1 = L293D [package=THT]
  Part1 = Arduino Uno (Rev3)
  M1 = DC Motor
  R1 = PHOTOCELL [package=photocell-kit]
  R2 = PHOTOCELL [package=photocell-kit]
  M2 = DC Motor
  R2_2 = Resistor [tolerance=±5% resistance=10k package=THT]
  R1_2 = Resistor [tolerance=±5% resistance=10k package=THT]
  BAT1 = BC9VPC [package=bc9vpc]  # not connected

nets:
  N1: IC1.Enable_1, IC1.Enable_2, Part1.D9_PWM
  N2: IC1.In_1, Part1.D3_PWM
  N3: IC1.Out_1_(_Controlled_by_Enable_1_), M1.pin_2
  N4: IC1.0V, Part1.GND, R2_2.Pin_0, R1_2.Pin_0
  N5: IC1.Out_2_(_Controlled_by_Enable_1_), M1.pin_1
  N6: IC1.In_2, Part1.D4
  N7: IC1.+Vmotor, Part1.VIN
  N8: IC1.In_3, Part1.D6_PWM
  N9: IC1.Out_3_(_Controlled_by_Enable_2_), M2.pin_1
  N10: IC1.Out_4_(_Controlled_by_Enable_2_), M2.pin_2
  N11: IC1.In_4, Part1.D5_PWM
  N12: Part1.A0, R1.P$1, R2_2.Pin_1
  N13: Part1.A1, R2.P$1, R1_2.Pin_1
  N14: Part1.5V, R1.P$2, R2.P$2
