# Fritzing sketch Robot1_H-Bridge_Wiring (saved by Fritzing 0.9.2b)
breadboards: 1

parts:
  IC1 = L293D [package=THT]
  Part1 = Arduino Uno (Rev3)
  M1 = DC Motor
  VCC1 = 4 x AAA Battery Mount
  M2 = DC Motor

nets:
  N1: IC1.Enable_1, IC1.Enable_2, Part1.D9_PWM
  N2: IC1.In_1, Part1.D3_PWM
  N3: IC1.Out_1_(_Controlled_by_Enable_1_), M1.pin_2
  N4: IC1.0V, Part1.GND, VCC1.-
  N5: IC1.Out_2_(_Controlled_by_Enable_1_), M1.pin_1
  N6: IC1.In_2, Part1.D4
  N7: IC1.+Vmotor, Part1.VIN, VCC1.+
  N8: IC1.In_3, Part1.D6_PWM
  N9: IC1.Out_3_(_Controlled_by_Enable_2_), M2.pin_1
  N10: IC1.Out_4_(_Controlled_by_Enable_2_), M2.pin_2
  N11: IC1.In_4, Part1.D5_PWM
